// Digital circuit PatternRecognizerMikroprogrammiertSolution.dig as structural Verilog
module PatternRecognizerMikroprogrammiertSolution (
  input  I,
  input  clk,
  output O
);

  wire [1:0] FF0_q;
  wire [2:1] rom_1_d;

  ROM #(.AddrBits(3), .Bits(3)) rom_1 (.A({I, FF0_q}), .sel(1'b1), .D({rom_1_d, O}));
  D_FF FF1 (.D(rom_1_d[2]), .C(clk), .Q(FF0_q[1]));  // open: nQ
  D_FF FF0 (.D(rom_1_d[1]), .C(clk), .Q(FF0_q[0]));  // open: nQ

  // Notes on the sheet:
  //   contents of rom_1 (hex, n*v repeats v):
  //   0,4,0,5,2,2,6,3
endmodule

/* Test case TestAutomat:
clk I FF1 FF0 O
init FF1=0;
init FF0=0;
0 0 0 0 0
C 0 0 0 0
C 1 0 1 0
C 1 0 1 0
C 0 1 0 0
C 0 0 0 0
C 1 0 1 0
C 0 1 0 0
C 1 1 1 1
C 0 1 0 0
C 1 1 1 1
C 1 0 1 0
*/
