// Digital circuit PatternRecognizerMikroprogrammiertTemplate.dig as structural Verilog
module PatternRecognizerMikroprogrammiertTemplate (
  input  I,
  input  clk,
  output O
);

  wire FF0_q, FF1_q, undriven, undriven_2;

  D_FF FF1 (.D(undriven_2), .C(clk), .Q(FF1_q));  // open: nQ
  D_FF FF0 (.D(undriven), .C(clk), .Q(FF0_q));  // open: nQ
endmodule

/* Test case TestAutomat:
clk I FF1 FF0 O
init FF1=0;
init FF0=0;
0 0 0 0 0
C 0 0 0 0
C 1 0 1 0
C 1 0 1 0
C 0 1 0 0
C 0 0 0 0
C 1 0 1 0
C 0 1 0 0
C 1 1 1 1
C 0 1 0 0
C 1 1 1 1
C 1 0 1 0
*/
