// Digital circuit PatternRecognizerTemplate.dig as structural Verilog
module PatternRecognizerTemplate (
  input  I,
  input  clk,
  output O
);

  wire FF0_q, FF1_q, not_1_out, not_2_out;

  not not_1 (not_1_out, I);
  not not_2 (not_2_out, FF0_q);
  D_FF FF1 (.C(clk), .Q(FF1_q));  // open: D, nQ
  D_FF FF0 (.C(clk), .Q(FF0_q));  // open: D, nQ

  // Notes on the sheet:
  //   I ¬I
  //   FF1
  //   FF0 ¬FF0
endmodule

/* Test case TestAutomat:
clk I FF1 FF0 O
init FF1=0;
init FF0=0;
0 0 0 0 0
C 0 0 0 0
C 1 0 1 0
C 1 0 1 0
C 0 1 0 0
C 0 0 0 0
C 1 0 1 0
C 0 1 0 0
C 1 1 1 1
C 0 1 0 0
C 1 1 1 1
C 1 0 1 0
*/
